// Logisim project ep1.circ as structural Verilog: 3 circuits, main circuit main
module main (
  input  [7:0] in_1,
  input  OP,
  input  [7:0] in_3,
  output CS,
  output [7:0] out_5,
  output SS
);

  wire not_2_out, somador_1_c7, somador_1_c8;
  wire [7:0] multiplexer_1_out, not_1_out;

  Multiplexer #(.width(8)) multiplexer_1 (.in0(in_3), .in1(not_1_out), .out(multiplexer_1_out), .sel(OP));
  assign not_1_out = ~in_3;  // NOT_Gate not_1, 8 bits wide
  somador somador_1 (.A(in_1), .Cin(OP), .B(multiplexer_1_out), .c7(somador_1_c7), .c8(somador_1_c8), .S(out_5));
  not not_2 (not_2_out, somador_1_c8);
  xor xor_1 (CS, somador_1_c7, somador_1_c8);
  Multiplexer multiplexer_2 (.in0(somador_1_c8), .in1(not_2_out), .out(SS), .sel(OP));

  // Notes on the sheet:
  //   OP=0 ADICAO
  //   OP=1 SUBTRACAO
  //   overflow com sinal
  //   overflow sem sinal
endmodule

module somabits (
  input  a,
  input  b,
  input  Cin,
  output S,
  output Cout
);

  wire and_1_out, and_2_out, and_3_out, and_4_out, and_5_out, and_6_out, and_7_out, not_1_out, not_2_out,
       not_3_out;

  not not_1 (not_1_out, a);
  not not_2 (not_2_out, b);
  not not_3 (not_3_out, Cin);
  and and_1 (and_1_out, a, b, Cin);
  and and_2 (and_2_out, a, b, not_3_out);
  and and_3 (and_3_out, a, not_2_out, Cin);
  and and_4 (and_4_out, a, not_2_out, not_3_out);
  and and_5 (and_5_out, not_1_out, b, Cin);
  and and_6 (and_6_out, not_1_out, b, not_3_out);
  and and_7 (and_7_out, not_1_out, not_2_out, Cin);
  or or_1 (S, and_1_out, and_4_out, and_6_out, and_7_out);
  or or_2 (Cout, and_1_out, and_2_out, and_3_out, and_5_out);
endmodule

module somador (
  input  [7:0] A,
  input  Cin,
  input  [7:0] B,
  output c7,
  output c8,
  output [7:0] S
);

  wire somabits_3_cout, somabits_4_cout, somabits_5_cout, somabits_6_cout, somabits_7_cout, somabits_8_cout;

  somabits somabits_1 (.a(A[7]), .b(B[7]), .Cin(c7), .S(S[7]), .Cout(c8));
  somabits somabits_2 (.a(A[6]), .b(B[6]), .Cin(somabits_3_cout), .S(S[6]), .Cout(c7));
  somabits somabits_3 (.a(A[5]), .b(B[5]), .Cin(somabits_4_cout), .S(S[5]), .Cout(somabits_3_cout));
  somabits somabits_4 (.a(A[4]), .b(B[4]), .Cin(somabits_5_cout), .S(S[4]), .Cout(somabits_4_cout));
  somabits somabits_5 (.a(A[3]), .b(B[3]), .Cin(somabits_6_cout), .S(S[3]), .Cout(somabits_5_cout));
  somabits somabits_6 (.a(A[2]), .b(B[2]), .Cin(somabits_7_cout), .S(S[2]), .Cout(somabits_6_cout));
  somabits somabits_7 (.a(A[1]), .b(B[1]), .Cin(somabits_8_cout), .S(S[1]), .Cout(somabits_7_cout));
  somabits somabits_8 (.a(A[0]), .b(B[0]), .Cin(Cin), .S(S[0]), .Cout(somabits_8_cout));
endmodule
