// Logisim project ep1EnzoOliveira.circ as structural Verilog: 6 circuits, main circuit ep1
module ep1 (
  input  [7:0] A,
  input  OP,
  input  [7:0] B,
  output CS,
  output [7:0] out_5,
  output SS
);

  wire not_2_out, somador_1_c7, somador_1_c8;
  wire [7:0] multiplexer_1_out, not_1_out;

  Multiplexer #(.width(8)) multiplexer_1 (.in0(B), .in1(not_1_out), .out(multiplexer_1_out), .sel(OP));
  assign not_1_out = ~B;  // NOT_Gate not_1, 8 bits wide
  somador somador_1 (.A(A), .Cin(OP), .B(multiplexer_1_out), .c7(somador_1_c7), .c8(somador_1_c8), .S(out_5));
  not not_2 (not_2_out, somador_1_c8);
  xor xor_1 (CS, somador_1_c7, somador_1_c8);
  Multiplexer multiplexer_2 (.in0(somador_1_c8), .in1(not_2_out), .out(SS), .sel(OP));

  // Notes on the sheet:
  //   OP=0 ADICAO
  //   OP=1 SUBTRACAO
  //   overflow com sinal
  //   overflow sem sinal
endmodule

module somabits (
  input  a,
  input  b,
  input  Cin,
  output S,
  output Cout
);

  wire and_1_out, and_2_out, and_3_out, and_4_out, and_5_out, and_6_out, and_7_out, not_1_out, not_2_out,
       not_3_out;

  not not_1 (not_1_out, a);
  not not_2 (not_2_out, b);
  not not_3 (not_3_out, Cin);
  and and_1 (and_1_out, a, b, Cin);
  and and_2 (and_2_out, a, b, not_3_out);
  and and_3 (and_3_out, a, not_2_out, Cin);
  and and_4 (and_4_out, a, not_2_out, not_3_out);
  and and_5 (and_5_out, not_1_out, b, Cin);
  and and_6 (and_6_out, not_1_out, b, not_3_out);
  and and_7 (and_7_out, not_1_out, not_2_out, Cin);
  or or_1 (S, and_1_out, and_4_out, and_6_out, and_7_out);
  or or_2 (Cout, and_1_out, and_2_out, and_3_out, and_5_out);
endmodule

module somador (
  input  [7:0] A,
  input  Cin,
  input  [7:0] B,
  output c7,
  output c8,
  output [7:0] S
);

  wire somabits_3_cout, somabits_4_cout, somabits_5_cout, somabits_6_cout, somabits_7_cout, somabits_8_cout;

  somabits somabits_1 (.a(A[7]), .b(B[7]), .Cin(c7), .S(S[7]), .Cout(c8));
  somabits somabits_2 (.a(A[6]), .b(B[6]), .Cin(somabits_3_cout), .S(S[6]), .Cout(c7));
  somabits somabits_3 (.a(A[5]), .b(B[5]), .Cin(somabits_4_cout), .S(S[5]), .Cout(somabits_3_cout));
  somabits somabits_4 (.a(A[4]), .b(B[4]), .Cin(somabits_5_cout), .S(S[4]), .Cout(somabits_4_cout));
  somabits somabits_5 (.a(A[3]), .b(B[3]), .Cin(somabits_6_cout), .S(S[3]), .Cout(somabits_5_cout));
  somabits somabits_6 (.a(A[2]), .b(B[2]), .Cin(somabits_7_cout), .S(S[2]), .Cout(somabits_6_cout));
  somabits somabits_7 (.a(A[1]), .b(B[1]), .Cin(somabits_8_cout), .S(S[1]), .Cout(somabits_7_cout));
  somabits somabits_8 (.a(A[0]), .b(B[0]), .Cin(Cin), .S(S[0]), .Cout(somabits_8_cout));
endmodule

module comparador (
  input  [7:0] in_1,
  input  [7:0] in_2,
  output AeqB,
  output amenorqB,
  output aMaiorqB
);

  wire and_1_out, and_2_out, and_3_out, and_4_out, and_5_out, and_6_out, and_7_out, and_8_out, not_1_out,
       not_2_out, not_3_out, not_4_out, not_5_out, not_6_out, not_7_out, not_8_out, xnor_1_out, xnor_2_out,
       xnor_3_out, xnor_4_out, xnor_5_out, xnor_6_out, xnor_7_out, xnor_8_out;

  xnor xnor_1 (xnor_1_out, in_1[7], in_2[7]);
  xnor xnor_2 (xnor_2_out, in_1[6], in_2[6]);
  xnor xnor_3 (xnor_3_out, in_1[5], in_2[5]);
  xnor xnor_4 (xnor_4_out, in_1[4], in_2[4]);
  xnor xnor_5 (xnor_5_out, in_1[3], in_2[3]);
  xnor xnor_6 (xnor_6_out, in_1[2], in_2[2]);
  xnor xnor_7 (xnor_7_out, in_1[1], in_2[1]);
  xnor xnor_8 (xnor_8_out, in_1[0], in_2[0]);
  not not_1 (not_1_out, in_2[7]);
  not not_2 (not_2_out, in_2[6]);
  and and_1 (and_1_out, in_1[7], not_1_out);
  and and_2 (and_2_out, xnor_1_out, in_1[6], not_2_out);
  and and_3 (and_3_out, xnor_1_out, xnor_2_out, in_1[5], not_3_out);
  not not_3 (not_3_out, in_2[5]);
  and and_4 (and_4_out, xnor_1_out, xnor_2_out, xnor_3_out, in_1[4], not_4_out);
  not not_4 (not_4_out, in_2[4]);
  and and_5 (and_5_out, xnor_1_out, xnor_2_out, xnor_3_out, xnor_4_out, in_1[3], not_5_out);
  not not_5 (not_5_out, in_2[3]);
  and and_6 (and_6_out, xnor_1_out, xnor_2_out, xnor_3_out, xnor_4_out, xnor_5_out, in_1[2], not_6_out);
  not not_6 (not_6_out, in_2[2]);
  and and_7 (and_7_out, xnor_1_out, xnor_2_out, xnor_3_out, xnor_4_out, xnor_5_out, xnor_6_out, in_1[1], not_7_out);
  not not_7 (not_7_out, in_2[1]);
  and and_8 (and_8_out, xnor_1_out, xnor_2_out, xnor_3_out, xnor_4_out, xnor_5_out, xnor_6_out, xnor_7_out, in_1[0], not_8_out);
  not not_8 (not_8_out, in_2[0]);
  and and_9 (AeqB, xnor_1_out, xnor_2_out, xnor_3_out, xnor_4_out, xnor_5_out, xnor_6_out, xnor_7_out, xnor_8_out);
  or or_1 (aMaiorqB, and_1_out, and_2_out, and_3_out, and_5_out, and_6_out, and_4_out, and_7_out, and_8_out);
  nor nor_1 (amenorqB, aMaiorqB, AeqB);
endmodule

module ULA (
  input  [7:0] A,
  input  OP,
  input  [7:0] B,
  output o2,
  output o1,
  output c2,
  output c1,
  output c0,
  output c3,
  output c5,
  output c4
);

  wire and_1_out, and_2_out, comparador_3_amaiorqb, comparador_3_amenorqb, not_1_out, not_2_out, xor_1_out;

  ep1 ep1_1 (.A(A), .OP(OP), .B(B), .CS(o2), .SS(o1));  // open: out_5
  comparador comparador_1 (.in_1(A), .in_2(B), .AeqB(c2), .amenorqB(c1), .aMaiorqB(c0));
  comparador comparador_2 (.in_1(A), .in_2({8{1'b0}}), .AeqB(c3));  // open: amenorqB, aMaiorqB
  comparador comparador_3 (
    .in_1({1'b0, A[6:0]}), .in_2({1'b0, B[6:0]}), .amenorqB(comparador_3_amenorqb),
    .aMaiorqB(comparador_3_amaiorqb));  // open: AeqB
  and and_1 (and_1_out, not_1_out, B[7]);
  not not_1 (not_1_out, A[7]);
  Multiplexer multiplexer_1 (.in0(comparador_3_amaiorqb), .in1(and_1_out), .out(c4), .sel(xor_1_out));
  and and_2 (and_2_out, A[7], not_2_out);
  Multiplexer multiplexer_2 (.in0(comparador_3_amenorqb), .in1(and_2_out), .out(c5), .sel(xor_1_out));
  xor xor_1 (xor_1_out, B[7], A[7]);
  not not_2 (not_2_out, B[7]);
endmodule

module ep2 (
  input  [7:0] A,
  input  OP,
  input  [7:0] B,
  output o2,
  output o1,
  output c2,
  output c1,
  output c0,
  output c3,
  output c5,
  output c4
);

  ULA ula_1 (.A(A), .OP(OP), .B(B), .o2(o2), .o1(o1), .c2(c2), .c1(c1), .c0(c0), .c3(c3), .c5(c5), .c4(c4));
endmodule
